# Fritzing sketch 01_blink copy 2 (saved by Fritzing 0.9.2b)
breadboards: 1

parts:
  LED2 = LEDs [package=led10mm]
  R2 = Resistor [tolerance=±5% resistance=270 package=THT]
  MonkMakesDuino2 = MonkMakesDuino

nets:
  N1: LED2.A, MonkMakesDuino2.13
  N2: LED2.C, R2.Pin_0
  N3: R2.Pin_1, MonkMakesDuino2.GND

custom parts:
  LEDs: LEDs Standard schematic elements and footprints for 5mm, 3mm, 1206, and 0603 sized LEDs. 5mm - Spark Fun Electronics SKU : COM-00529 (and others)
