# Fritzing sketch 04 thermometer (saved by Fritzing 0.8.4b)
breadboards: 1

parts:
  R1 = Resistor [tolerance=±5% resistance=1k package=THT]
  R2 = Resistor [tolerance=±5% resistance=1k package=THT]
  Raspberry_Pi_rev1 = Raspberry Pi B rev2
  R3 = Temperature Sensor (Thermistor) [thermistor_type=NTC package=THT]
  C4 = Capacitor [package=cap-pth-small2]

nets:
  N1: R1.Pin_0, Raspberry_Pi_rev1.GPIO_18
  N2: R1.Pin_1, R3.pin_0
  N3: R2.Pin_0, Raspberry_Pi_rev1.GPIO_23
  N4: R2.Pin_1, Raspberry_Pi_rev1.GND, R3.pin_1, C4.1, C4.2
