# Fritzing sketch buzzer (saved by Fritzing 0.9.2b)
breadboards: 1

parts:
  MonkMakesDuino2 = MonkMakesDuino
  S3 = Piezo Buzzer

nets:
  N1: MonkMakesDuino2.13, S3.pin2
  N2: MonkMakesDuino2.GND, S3.pin1

custom parts:
  Piezo Buzzer: Piezo Buzzer (PCB Mount)
