# Fritzing sketch mosfet (saved by Fritzing 0.9.2b)
breadboards: 1

parts:
  MonkMakesDuino2 = MonkMakesDuino
  M1 = DC Motor
  Q1 = Basic FET N-Channel [package="D2Pak [SMD]"]

nets:
  N1: MonkMakesDuino2.9, Q1.Gate
  N2: MonkMakesDuino2.GND, Q1.source
  N3: MonkMakesDuino2.5V, M1.pin_1
  N4: M1.pin_2, Q1.drain
