# Fritzing sketch neopixel (saved by Fritzing 0.9.2b)
breadboards: 1

parts:
  MonkMakesDuino2 = MonkMakesDuino
  NEOPIXEL1 = Neopixel Strip -- Black (30/m)

nets:
  N1: MonkMakesDuino2.6, NEOPIXEL1.Din
  GND: MonkMakesDuino2.GND, NEOPIXEL1.GND
  5V: MonkMakesDuino2.5V, NEOPIXEL1.+5V

custom parts:
  Neopixel Strip -- Black (30/m): These NeoPixel strips have 30 digitally-addressable pixel LEDs per meter and are very affordable and are only 12.5 mm wide, 10 mm if you remove the strip from the casing.
