# Fritzing sketch push_switch (saved by Fritzing 0.9.2b)
breadboards: 1

parts:
  MonkMakesDuino2 = MonkMakesDuino
  S1 = Pushbutton [package="[THT]"]

nets:
  N1: MonkMakesDuino2.13, S1.Pin_3, S1.Pin_4
  N2: MonkMakesDuino2.GND, S1.Pin_1, S1.Pin_2
