# Fritzing sketch push_switch_and_led (saved by Fritzing 0.9.2b)
breadboards: 1

parts:
  MonkMakesDuino2 = MonkMakesDuino
  LED3 = LEDs [package=led10mm]
  R3 = Resistor [tolerance=±5% resistance=270 package=THT]
  S1 = Pushbutton [package="[THT]"]

nets:
  N1: MonkMakesDuino2.9, LED3.A
  N2: MonkMakesDuino2.13, S1.Pin_3, S1.Pin_4
  N3: MonkMakesDuino2.GND, R3.Pin_1, S1.Pin_1, S1.Pin_2
  N4: LED3.C, R3.Pin_0

custom parts:
  LEDs: LEDs Standard schematic elements and footprints for 5mm, 3mm, 1206, and 0603 sized LEDs. 5mm - Spark Fun Electronics SKU : COM-00529 (and others)
