# Fritzing sketch servos (saved by Fritzing 0.9.3b)
breadboards: 1

parts:
  MonkMakesDuino2 = MonkMakesDuino
  J1 = Basic Servo

nets:
  N1: MonkMakesDuino2.6, J1.pulse
  GND: MonkMakesDuino2.GND, J1.gnd
  5V: MonkMakesDuino2.5V, J1.vcc
