# Fritzing sketch speaker (saved by Fritzing 0.9.3b)
breadboards: 1

parts:
  MonkMakesDuino2 = MonkMakesDuino
  SPKR1 = Loudspeaker

nets:
  N1: MonkMakesDuino2.9, SPKR1.pin2
  N2: MonkMakesDuino2.GND, SPKR1.pin1
