# Fritzing sketch thermistor (saved by Fritzing 0.9.2b)
breadboards: 1

parts:
  MonkMakesDuino2 = MonkMakesDuino
  R4 = Temperature Sensor (Thermistor) [thermistor_type=NTC package=THT]
  R5 = Resistor [tolerance=±5% resistance=1k package=THT]

nets:
  N1: MonkMakesDuino2.A0, R4.pin_1, R5.Pin_0
  N2: MonkMakesDuino2.GND, R5.Pin_1
  N3: MonkMakesDuino2.5V, R4.pin_0
